// Logisim project prelab7circ.circ as structural Verilog: 1 circuit, main circuit main
module main (
);

  wire instrument_cluster_1_p3, instrument_cluster_1_p4, sn74hc541n_1_p1, sn74hc541n_1_p4, sn74hc541n_1_p8,
       sn74hc541n_1_p9;

  // Discovery_P1_Connector discovery_p1_connector_1: pin names not known
  // SN74HC541N sn74hc541n_1: pin names not known; wires that end beside it: sn74hc541n_1_p1, 1'b0, sn74hc541n_1_p1, sn74hc541n_1_p4, 1'b0, 1'b1, 1'b0, sn74hc541n_1_p8, sn74hc541n_1_p9
  // CAN_Transceiver can_transceiver_1: pin names not known; wires that end beside it: 1'b1, 1'b0, sn74hc541n_1_p8, sn74hc541n_1_p9
  // Instrument_Cluster instrument_cluster_1: pin names not known; wires that end beside it: 1'b1, 1'b0, instrument_cluster_1_p3, instrument_cluster_1_p4, 1'b1, instrument_cluster_1_p4

  // Notes on the sheet:
  //   3.3V
  //   12V
  //   12V
endmodule
